// Logisim project 24decode_en.circ as structural Verilog: 1 circuit, main circuit main
module main (
  input  A,
  input  B,
  input  En
);

  wire nand_1_out, nand_2_out, nand_3_out, nand_4_out, not_1_out, not_2_out, not_3_out;

  not not_1 (not_1_out, A);
  not not_2 (not_2_out, B);
  not not_3 (not_3_out, En);
  nand nand_1 (nand_1_out, not_1_out, not_3_out, not_2_out);
  nand nand_2 (nand_2_out, not_1_out, not_3_out, B);
  nand nand_3 (nand_3_out, A, not_3_out, not_2_out);
  nand nand_4 (nand_4_out, A, not_3_out, B);
  // Probe on nand_1_out
  // Probe on nand_2_out
  // Probe on nand_3_out
  // Probe on nand_4_out
endmodule
